# Fritzing sketch waterflow (saved by Fritzing 0.9.3b)
breadboards: 1

parts:
  Composant1 = Arduino Uno (Rev3)
  R1 = Resistor [tolerance=±5% resistance=220 package="2512 [SMD]"]

nets:
  N1: Composant1.D2, R1.Pin_1
  N2: Composant1.5V, R1.Pin_0
